// Logisim project use_me.circ as structural Verilog: 2 circuits, main circuit fa
module fa (
  input  cin,
  input  a,
  input  b,
  output out_4,
  output cou
);

  wire and_1_out, and_2_out, xor_1_out;

  xor xor_1 (xor_1_out, a, b);
  xor xor_2 (out_4, xor_1_out, cin);
  and and_1 (and_1_out, cin, xor_1_out);
  and and_2 (and_2_out, b, a);
  or or_1 (cou, and_1_out, and_1_out, and_2_out);
endmodule

module rca (
  input  [3:0] A,
  input  [3:0] B,
  output [3:0] s,
  output cou
);

  wire fa_1_cou, fa_2_cou, fa_3_cou;

  fa fa_1 (.cin(1'b0), .a(A[0]), .b(B[0]), .out_4(s[0]), .cou(fa_1_cou));
  fa fa_2 (.cin(fa_1_cou), .a(A[1]), .b(B[1]), .out_4(s[1]), .cou(fa_2_cou));
  fa fa_3 (.cin(fa_2_cou), .a(A[2]), .b(B[2]), .out_4(s[2]), .cou(fa_3_cou));
  fa fa_4 (.cin(fa_3_cou), .a(A[3]), .b(B[3]), .out_4(s[3]), .cou(cou));
endmodule
